// Logisim project SecoV_V2.2.circ as structural Verilog: 10 circuits, main circuit CPU
module CPU (
);

  wire alu_a_mux, alu_b_mux, clk, data_memory_wr_en, pc_alu_a_mux, pc_alu_b_mux, register_wr_en;
  wire [1:0] data_memory_i_mux, register_c_mux;
  wire [2:0] alu_comparison, expander_imm_select, expander_load_select;
  wire [3:0] alu_select;
  wire [4:0] rd_instruction, rs1_instruction, rs2_instruction;
  wire [31:0] data_memory_i, instruction, multiplexer_2_out, multiplexer_3_out, multiplexer_4_out,
       multiplexer_5_out, multiplexer_6_out, pc_alu_o, peripheral, register_a_data, sext_register_b_data_8,
       sext_register_b_data_16, undriven, undriven_2, undriven_3, undriven_4, undriven_5, undriven_6,
       undriven_7, undriven_8;

  controller controller_1 (
    .instruction_i(instruction), .alu_comparison_i(alu_comparison), .rs1_instruction_o(rs1_instruction),
    .rs2_instruction_o(rs2_instruction), .rd_instruction_o(rd_instruction),
    .register_wr_en_o(register_wr_en), .alu_select_o(alu_select), .alu_a_mux_o(alu_a_mux),
    .alu_b_mux_o(alu_b_mux), .register_c_mux_o(register_c_mux), .data_memory_wr_en_o(data_memory_wr_en),
    .data_memory_i_mux(data_memory_i_mux), .pc_alu_a_mux_o(pc_alu_a_mux), .pc_alu_b_mux_o(pc_alu_b_mux),
    .expander_imm_select(expander_imm_select), .expander_load_select(expander_load_select));
  Registers registers_1 (
    .wr_en_i(register_wr_en), .clk(clk), .a_address_i(rs1_instruction), .b_address_i(rs2_instruction),
    .c_address_i(rd_instruction), .c_data_i(multiplexer_5_out), .a_data_o(register_a_data),
    .b_data_o(undriven));
  expander expander_1 (.intstruction_i(instruction), .immediate_select_i(expander_imm_select), .data_o(undriven_2));
  Multiplexer #(.select(2), .width(32)) multiplexer_1 (
    .in0(undriven), .in1(sext_register_b_data_16), .in2(sext_register_b_data_8), .in3({32{1'b0}}),
    .out(data_memory_i), .sel(data_memory_i_mux));
  Multiplexer #(.width(32)) multiplexer_2 (
    .in0(register_a_data), .in1(pc_alu_o), .out(multiplexer_2_out), .sel(alu_a_mux));
  Multiplexer #(.width(32)) multiplexer_3 (.in0(undriven), .in1(undriven_2), .out(multiplexer_3_out), .sel(alu_b_mux));
  Multiplexer #(.width(32)) multiplexer_4 (.in0(32'h4), .in1(undriven_2), .out(multiplexer_4_out), .sel(pc_alu_a_mux));
  ALU alu_1 (
    .comparison_o(alu_comparison), .select_i(alu_select), .data_o(undriven_6), .a_i(multiplexer_2_out),
    .b_i(multiplexer_3_out));
  pc_adder pc_adder_1 (.ALU_o(undriven_3), .ALU_A(multiplexer_4_out), .ALU_B(multiplexer_6_out));
  Multiplexer #(.select(2), .width(32)) multiplexer_5 (
    .in0(undriven_6), .in1(undriven_4), .in2(undriven_5), .in3(undriven_2), .out(multiplexer_5_out),
    .sel(register_c_mux));
  pc_register pc_register_1 (.data_i(undriven_3), .data_o(undriven_7), .clk(clk));
  Multiplexer #(.width(32)) multiplexer_6 (
    .in0(undriven_7), .in1(register_a_data), .out(multiplexer_6_out), .sel(pc_alu_b_mux));
  pc_adder pc_adder_2 (.ALU_o(undriven_5), .ALU_A(32'h4), .ALU_B(undriven_7));
  program_memory program_memory_1 (.address(undriven_7), .data_o(instruction));
  data_memory data_memory_1 (
    .address(undriven_6), .data_i(data_memory_i), .wr_en(data_memory_wr_en), .clk(clk), .data_o(undriven_8),
    .peripheral_io(peripheral));
  expander_load expander_load_1 (.data_i(undriven_8), .select_i(expander_load_select), .data_o(undriven_4));

  // Notes on the sheet:
  //   register_c_data
  //   register_b_data
  //   register_a_data
  //   expander_data
  //   register_b_data
  //   expander_data
  //   alu_a
  //   alu_b
  //   register_c_data
  //   pc_alu_a_i
  //   pc_alu_b_i
  //   alu_o
  //   expander_data_o
  //   pc_alu_o
  //   pc
  //   alu_o
  //   pc_plus_four
  //   expander_load_data
  //   pc
  //   pc
  //   data_memory_o
  //   SecoV
  //   V2.2.4.1
endmodule

module ALU (
  input  [31:0] data_o,
  input  [31:0] a_i,
  input  [31:0] b_i,
  input  [3:0] select_i,
  input  [2:0] comparison_o
);
endmodule

module Registers (
  input  [4:0] a_address_i,
  input  [31:0] a_data_o,
  input  [4:0] b_address_i,
  input  [4:0] c_address_i,
  input  [31:0] b_data_o,
  input  [31:0] c_data_i,
  input  wr_en_i,
  input  clk
);
endmodule

module expander (
  input  [31:0] intstruction_i,
  input  [31:0] data_o,
  input  [2:0] immediate_select_i
);
endmodule

module data_memory (
  input  [31:0] address,
  input  [31:0] data_o,
  input  [31:0] data_i,
  input  [31:0] peripheral_io,
  input  wr_en,
  input  clk
);
endmodule

module program_memory (
  input  [31:0] address,
  input  [31:0] data_o
);
endmodule

module controller (
  input  [31:0] instruction_i,
  input  register_wr_en_o,
  input  [3:0] alu_select_o,
  input  alu_a_mux_o,
  input  alu_b_mux_o,
  input  [2:0] alu_comparison_i,
  input  [1:0] register_c_mux_o,
  input  data_memory_wr_en_o,
  input  [1:0] data_memory_i_mux,
  input  pc_alu_a_mux_o,
  input  pc_alu_b_mux_o,
  input  [2:0] expander_imm_select,
  input  [4:0] rs1_instruction_o,
  input  [4:0] rs2_instruction_o,
  input  [4:0] rd_instruction_o,
  input  [2:0] expander_load_select
);
endmodule

module pc_adder (
  input  [31:0] ALU_o,
  input  [31:0] ALU_A,
  input  [31:0] ALU_B
);
endmodule

module expander_load (
  input  [31:0] data_i,
  input  [31:0] data_o,
  input  [2:0] select_i
);
endmodule

module pc_register (
  input  [31:0] data_i,
  input  [31:0] data_o,
  input  clk
);
endmodule
